// Digital circuit Control Unit.dig as structural Verilog
module Control_Unit (
  input  [15:0] IR,
  input  R,
  input  I,
  input  IEN,
  input  E,
  input  FGI,
  input  FGO,
  input  [15:0] AC,
  input  CLK,
  input  S,
  input  [15:0] DR,
  input  C_OUT,
  output [6:0] X,
  output S_clr,
  output IEN_J,
  output IEN_K,
  output FGI_K,
  output FGO_K,
  output AR_LD,
  output AR_INR,
  output AR_CLR,
  output MEM_read,
  output MEM_write,
  output PC_LD,
  output PC_INCR,
  output PC_CLR,
  output DR_LD,
  output DR_INCR,
  output AC_LD,
  output AC_INCR,
  output AC_CLR,
  output [6:0] AL_OP,
  output OUTR_LD,
  output IR_LD,
  output TR_LD,
  output [15:0] T,
  output [7:0] D,
  output E_J,
  output E_K,
  output R_J,
  output R_K,
  output I_LD,
  output I_D
);

  wire add, \and , and_1_out, and_2_out, and_3_out, and_4_out, and_5_out, and_6_out, and_7_out, and_8_out,
       and_14_out, and_15_out, and_16_out, and_17_out, and_18_out, and_19_out, and_21_out, and_22_out,
       and_23_out, and_24_out, and_25_out, and_26_out, and_27_out, and_28_out, and_29_out, and_30_out,
       and_31_out, and_32_out, and_33_out, and_34_out, and_35_out, and_38_out, and_39_out, and_40_out,
       and_54_out, and_55_out, and_56_out, and_57_out, and_58_out, and_59_out, and_62_out, and_63_out,
       and_64_out, and_65_out, and_66_out, and_67_out, and_68_out, and_69_out, and_70_out, and_71_out, com,
       comparator_1_eq, comparator_2_eq, dr_t, or_1_out, or_10_out, or_12_out, or_13_out, or_18_out,
       or_19_out, p, r_t, shl, shr, \ınpr ;
  wire [2:0] priorityencoder_1_num;
  wire [3:0] SC_out;

  and and_1 (and_1_out, T[5], D[5]);
  and and_2 (and_2_out, D[4], T[4]);
  and and_3 (and_3_out, ~R, T[0]);  // And
  and and_4 (and_4_out, R, T[0]);
  and and_5 (and_5_out, D[5], T[4]);
  and and_6 (and_6_out, ~D[7], I, T[3]);  // And
  and and_7 (and_7_out, T[2], ~R);  // And
  and and_8 (and_8_out, ~R, T[0]);  // And
  and and_9 (AR_INR, D[5], T[4]);
  and and_10 (AR_CLR, T[0], R);
  and and_11 (PC_CLR, R, T[1]);
  and and_12 (r_t, D[7], ~I, T[3]);  // And
  or or_1 (or_1_out, FGI, FGO);
  or or_2 (X[0], and_1_out, and_2_out);
  or or_3 (X[1], and_3_out, and_4_out, and_5_out);
  Decoder #(.Selector_Bits(3)) decoder_1 (
    .sel(IR[14:12]), .out_0(D[0]), .out_1(D[1]), .out_2(D[2]), .out_3(D[3]), .out_4(D[4]), .out_5(D[5]),
    .out_6(D[6]), .out_7(D[7]));
  and and_13 (R_J, ~T[0], ~T[1], ~T[2], IEN, or_1_out);  // And
  or or_4 (AR_LD, and_6_out, and_7_out, and_8_out);
  Comparator #(.Bits(16)) comparator_1 (.a(AC), .b({16{1'b0}}), .eq(comparator_1_eq));  // open: gt, lt
  Comparator #(.Bits(16)) comparator_2 (.a(DR), .b({16{1'b0}}), .eq(comparator_2_eq));  // open: gt, lt
  and and_14 (and_14_out, D[1], T[5], C_OUT);
  and and_15 (and_15_out, D[1], T[5], ~C_OUT);  // And
  and and_16 (and_16_out, r_t, IR[7], AC[0]);
  and and_17 (and_17_out, r_t, IR[7], ~AC[0]);  // And
  and and_18 (and_18_out, r_t, IR[6], AC[15]);
  and and_19 (and_19_out, r_t, IR[6], ~AC[15]);  // And
  and and_20 (R_K, R, T[2]);
  and and_21 (and_21_out, T[5], D[2]);
  and and_22 (and_22_out, D[6], T[6]);
  and and_23 (and_23_out, D[3], T[4]);
  and and_24 (and_24_out, p, IR[10]);
  and and_25 (and_25_out, IR[3], r_t, AC[15]);
  and and_26 (and_26_out, ~AC[15], r_t, IR[4]);  // And
  and and_27 (and_27_out, r_t, IR[2], comparator_1_eq);
  and and_28 (and_28_out, ~E, r_t, IR[1]);  // And
  and and_29 (and_29_out, D[6], comparator_2_eq, T[6]);
  and and_30 (and_30_out, ~R, T[1]);  // And
  and and_31 (and_31_out, R, T[2]);
  and and_32 (and_32_out, FGI, IR[9], p);
  and and_33 (and_33_out, FGO, IR[8], p);
  or or_5 (X[2], and_21_out, and_22_out);
  or or_6 (X[3], and_23_out, and_24_out);
  and and_34 (and_34_out, r_t, IR[8]);
  and and_35 (and_35_out, r_t, IR[10]);
  or or_7 (E_J, and_14_out, and_16_out, and_18_out, and_34_out);
  and and_36 (X[4], ~R, T[2]);  // And
  and and_37 (X[5], R, T[1]);
  or or_8 (PC_INCR, and_25_out, and_26_out, and_27_out, and_28_out, and_29_out, and_30_out, and_31_out, and_32_out, and_33_out);
  or or_9 (E_K, and_15_out, and_17_out, and_19_out, and_34_out, and_35_out);
  and and_38 (and_38_out, ~D[7], I, T[3]);  // And
  and and_39 (and_39_out, ~R, T[1]);  // And
  or or_10 (or_10_out, D[1], D[0], D[2], D[6]);
  and and_40 (and_40_out, or_10_out, T[4]);
  or or_11 (MEM_read, and_38_out, and_39_out, and_40_out);
  and and_41 (\and , D[0], T[5]);
  and and_42 (add, D[1], T[5]);
  and and_43 (dr_t, D[2], T[5]);
  and and_44 (\ınpr , p, IR[11]);
  and and_45 (com, r_t, IR[9]);
  and and_46 (shr, r_t, IR[7]);
  and and_47 (shl, r_t, IR[6]);
  and and_48 (AC_INCR, r_t, IR[5]);
  and and_49 (AC_CLR, r_t, IR[11]);
  and and_50 (S_clr, r_t, IR[0]);
  or or_12 (or_12_out, D[1], D[0], D[2], D[6]);
  and and_51 (DR_LD, or_12_out, T[4]);
  and and_52 (DR_INCR, D[6], T[5]);
  and and_53 (I_LD, T[2], ~r_t);  // And
  or or_13 (or_13_out, \and , add, dr_t, \ınpr , com);
  and and_54 (and_54_out, R, T[1]);
  and and_55 (and_55_out, D[3], T[4]);
  and and_56 (and_56_out, D[5], T[4]);
  and and_57 (and_57_out, D[6], T[6]);
  and and_58 (and_58_out, T[5], D[5]);
  and and_59 (and_59_out, D[4], T[4]);
  or or_14 (AC_LD, or_13_out, shr, shl);
  PriorityEncoder #(.Selector_Bits(3)) priorityencoder_1 (
    .in0(shl), .in1(shr), .in2(com), .in3(\ınpr ), .in4(dr_t), .in5(add), .in6(\and ), .in7(1'b0),
    .num(priorityencoder_1_num));  // open: any
  or or_15 (MEM_write, and_54_out, and_55_out, and_56_out, and_57_out);
  or or_16 (PC_LD, and_58_out, and_59_out);
  Demultiplexer #(.Selector_Bits(3)) demultiplexer_1 (
    .sel(priorityencoder_1_num), .in(1'b1), .out_0(AL_OP[6]), .out_1(AL_OP[5]), .out_2(AL_OP[4]),
    .out_3(AL_OP[3]), .out_4(AL_OP[2]), .out_5(AL_OP[1]), .out_6(AL_OP[0]));  // open: out_7
  and and_60 (p, D[7], I, T[3]);
  and and_61 (IEN_J, p, IR[7]);
  and and_62 (and_62_out, p, IR[6]);
  and and_63 (and_63_out, R, T[2]);
  or or_17 (IEN_K, and_62_out, and_63_out);
  and and_64 (and_64_out, D[3], T[4]);
  and and_65 (and_65_out, R, T[2]);
  and and_66 (and_66_out, D[0], T[5]);
  and and_67 (and_67_out, D[1], T[5]);
  and and_68 (and_68_out, D[2], T[5]);
  and and_69 (and_69_out, T[5], D[5]);
  and and_70 (and_70_out, D[4], T[4]);
  and and_71 (and_71_out, D[6], T[6]);
  and and_72 (OUTR_LD, p, IR[10]);
  and and_73 (IR_LD, ~R, T[1]);  // And
  and and_74 (TR_LD, R, T[0]);
  or or_18 (or_18_out, and_64_out, and_65_out, and_66_out, and_67_out, and_68_out);
  or or_19 (or_19_out, or_18_out, r_t, p, and_69_out, and_70_out, and_71_out);
  and and_75 (FGI_K, p, IR[11]);
  and and_76 (FGO_K, p, IR[10]);
  Counter #(.Bits(4)) SC (.en(S), .C(CLK), .clr(or_19_out), .out(SC_out));  // open: ovf
  Decoder #(.Selector_Bits(4)) decoder_2 (
    .sel(SC_out), .out_0(T[0]), .out_1(T[1]), .out_2(T[2]), .out_3(T[3]), .out_4(T[4]), .out_5(T[5]),
    .out_6(T[6]), .out_7(T[7]), .out_8(T[8]), .out_9(T[9]), .out_10(T[10]), .out_11(T[11]), .out_12(T[12]),
    .out_13(T[13]), .out_14(T[14]), .out_15(T[15]));

  assign I_D = IR[15];
  assign X[6] = MEM_read;

  // Other names for the same wires on the sheet: alop[6:0] = AL_OP; accl = AC_CLR; acinc = AC_INCR; acload = AC_LD;
  //   arcl = AR_CLR; arld = AR_LD; arınc = AR_INR; COUT = C_OUT; drinc = DR_INCR; drld = DR_LD; ej = E_J; ek = E_K;
  //   fgok = FGO_K; fgık = FGI_K; IENINPUT = IEN; b0 = IR[0]; b1 = IR[1]; b2 = IR[2]; b3 = IR[3]; b4 = IR[4];
  //   b5 = IR[5]; b6 = IR[6]; b7 = IR[7]; b8 = IR[8]; b9 = IR[9]; b10 = IR[10]; b11 = IR[11]; d_t[2:0] = IR[14:12];
  //   ıd = IR[15]; memw = MEM_write; outr = OUTR_LD; pccl = PC_CLR; pcinc = PC_INCR; pcld = PC_LD; rj = R_J; rk = R_K;
  //   sclr = S_clr; tr = TR_LD; x1 = X[0]; x2 = X[1]; x3 = X[2]; x4 = X[3]; x5 = X[4]; x6 = X[5]; memr = MEM_read;
  //   x7 = MEM_read; ı = I; ıenj = IEN_J; ıenk = IEN_K; ıld = I_LD; ır = IR_LD

  // Notes on the sheet:
  //   İnput
  //   BUS
  //   AR
  //   PCincrement
  //   PCclear
  //   IR decoder
  //   E
  //   R
  //   M[read]
  //   DR
  //   AC
  //   Sclear
  //   I
  //   M[write]
  //   PCload
  //   IEN
  //   OUTR
  //   IR
  //   TR
  //   sequence counter
  //   FGI, FGO
  //   Outputs
endmodule
